// Logisim project cpu.circ as structural Verilog
// ALU
module alu (
  input  [15:0] Source,
  input  [15:0] Destination,
  input  [3:0] Op,
  output [15:0] Out,
  output Zero
);

  wire [15:0] adder_1_out, adder_2_out, nand_1_out, negator_1_out, shifter_1_out, shifter_2_out,
       subtractor_1_out, subtractor_2_out;

  Shifter #(.width(16), .shift("lr")) shifter_1 (.in(Source), .\dist (4'b0001), .out(shifter_1_out));
  Shifter #(.width(16)) shifter_2 (.in(Source), .\dist (4'b0001), .out(shifter_2_out));
  Adder #(.width(16)) adder_1 (.a(Destination), .b(Source), .out(adder_1_out), .cin(1'b0));  // open: cout
  Subtractor #(.width(16)) subtractor_1 (
    .a(Destination), .b(Source), .out(subtractor_1_out), .bin(1'b0));  // open: bout
  assign nand_1_out = ~(Destination & Source);  // NAND_Gate nand_1, 16 bits wide
  Negator #(.width(16)) negator_1 (.in(Source), .out(negator_1_out));
  Adder #(.width(16)) adder_2 (.a(Source), .b(16'h1), .out(adder_2_out));  // open: cin, cout
  Subtractor #(.width(16)) subtractor_2 (.a(Source), .b(16'h1), .out(subtractor_2_out));  // open: bin, bout
  Multiplexer #(.select(4), .width(16), .enable("false")) multiplexer_1 (
    .in0(shifter_1_out), .in1(shifter_2_out), .in2(adder_1_out), .in3(subtractor_1_out), .in4(nand_1_out),
    .in5(negator_1_out), .in6({16{1'b0}}), .in7(16'h1), .in8(Source), .in9(adder_2_out),
    .in10(subtractor_2_out), .out(Out), .sel(Op));  // open: in11, in12, in13, in14, in15
  nor nor_1 (Zero, 1'b0, Out[15], Out[14], Out[13], Out[12], Out[11], Out[10], Out[9], Out[8], Out[7], Out[6], Out[5], Out[4], Out[3], Out[2], Out[1], Out[0]);
endmodule

// Regs
module register_bank (
  input  WEn,
  input  [15:0] DstIn,
  input  Clk,
  input  [2:0] DstSel,
  input  [2:0] SrcSel,
  output [15:0] DstOut,
  output [15:0] SrcOut,
  output [15:0] IP,
  output [15:0] SP
);

  wire demultiplexer_1_out0, demultiplexer_1_out1, demultiplexer_1_out2, demultiplexer_1_out3,
       demultiplexer_1_out4, demultiplexer_1_out5, demultiplexer_1_out6, demultiplexer_1_out7, not_1_out,
       not_2_out, not_3_out, not_4_out, not_5_out, not_6_out, not_7_out, not_8_out, undriven, undriven_3;
  wire [15:0] register_1_q, register_2_q, register_3_q, register_4_q, register_6_q, register_7_q, undriven_2;

  Demultiplexer #(.select(3)) demultiplexer_1 (
    .out0(demultiplexer_1_out0), .out1(demultiplexer_1_out1), .out2(demultiplexer_1_out2),
    .out3(demultiplexer_1_out3), .out4(demultiplexer_1_out4), .out5(demultiplexer_1_out5),
    .out6(demultiplexer_1_out6), .out7(demultiplexer_1_out7), .in(WEn), .sel(DstSel));  // open: en
  Multiplexer #(.select(3), .width(16)) multiplexer_1 (
    .in0(IP), .in1(SP), .in2(register_1_q), .in3(register_2_q), .in4(register_3_q), .in5(register_4_q),
    .in6(register_6_q), .in7(undriven_2), .out(DstOut), .sel(DstSel), .en(undriven));
  Multiplexer #(.select(3), .width(16)) multiplexer_2 (
    .in0(IP), .in1(SP), .in2(register_1_q), .in3(register_2_q), .in4(register_3_q), .in5(register_4_q),
    .in6(register_6_q), .in7(undriven_2), .out(DstOut), .sel(DstSel), .en(undriven));
  not not_1 (not_1_out, demultiplexer_1_out0);
  not not_2 (not_2_out, demultiplexer_1_out1);
  Register #(.width(16)) u_IP (.D(DstIn), .en(not_1_out), .Q(IP), .clk(Clk));  // open: clr
  Multiplexer #(.select(3), .width(16)) multiplexer_3 (
    .in0(IP), .in1(SP), .in2(register_1_q), .in3(register_2_q), .in4(register_3_q), .in5(register_4_q),
    .in6(register_6_q), .in7(register_7_q), .out(SrcOut), .sel(SrcSel));  // open: en
  not not_3 (not_3_out, demultiplexer_1_out2);
  Register #(.width(16)) u_SP (.D(DstIn), .en(not_2_out), .Q(SP), .clk(Clk));  // open: clr
  not not_4 (not_4_out, demultiplexer_1_out3);
  Register #(.width(16)) register_1 (.D(DstIn), .en(not_3_out), .Q(register_1_q), .clk(Clk));  // open: clr
  not not_5 (not_5_out, demultiplexer_1_out4);
  Register #(.width(16)) register_2 (.D(DstIn), .en(not_4_out), .Q(register_2_q), .clk(Clk));  // open: clr
  Register #(.width(16)) register_3 (.D(DstIn), .en(not_5_out), .Q(register_3_q), .clk(Clk));  // open: clr
  not not_6 (not_6_out, demultiplexer_1_out5);
  Register #(.width(16)) register_4 (.D(DstIn), .en(not_6_out), .Q(register_4_q), .clk(Clk), .clr(undriven_3));
  Register #(.width(16)) register_5 (.D(DstIn), .en(not_6_out), .Q(register_4_q), .clk(Clk), .clr(undriven_3));
  not not_7 (not_7_out, demultiplexer_1_out6);
  Register #(.width(16)) register_6 (.D(DstIn), .en(not_7_out), .Q(register_6_q), .clk(Clk));  // open: clr
  not not_8 (not_8_out, demultiplexer_1_out7);
  Register #(.width(16)) register_7 (.D(DstIn), .en(not_8_out), .Q(register_7_q), .clk(Clk));  // open: clr
endmodule

// Ctrl
module cpu_controller (
  input  [15:0] IP,
  input  [15:0] Inst,
  output Clk,
  output RegsWEn,
  output [2:0] SrcSel,
  output [2:0] DstSel,
  output [3:0] AluOp,
  output [1:0] MemCtrl,
  output [15:0] Addr,
  output MemClk
);

  Register #(.width(16)) register_1 (.D(Inst));  // open: en, Q, clk, clr
  Register #(.width(16)) register_2 (.D(Inst));  // open: en, Q, clk, clr

  assign Addr = IP;
endmodule

module cpu (
  input  Clk,
  output [15:0] InstData,
  output [15:0] InstAddr,
  output [15:0] DataData,
  output InstClk,
  output [15:0] DataAddr,
  output [1:0] DataCtrl
);

  wire cpu_controller_1_regswen, not_1_out;
  wire [2:0] cpu_controller_1_dstsel, cpu_controller_1_srcsel;
  wire [3:0] cpu_controller_1_aluop;
  wire [15:0] alu_1_out, register_bank_1_dstout, register_bank_1_ip;

  not not_1 (not_1_out, Clk);
  register_bank register_bank_1 (
    .WEn(cpu_controller_1_regswen), .DstIn(DataData), .Clk(not_1_out), .SrcSel(cpu_controller_1_srcsel),
    .DstOut(register_bank_1_dstout), .SrcOut(DataAddr), .IP(register_bank_1_ip),
    .DstSel(cpu_controller_1_dstsel));  // open: SP
  cpu_controller cpu_controller_1 (
    .Clk(Clk), .IP(register_bank_1_ip), .Inst(InstData), .Addr(InstAddr), .MemClk(InstClk),
    .RegsWEn(cpu_controller_1_regswen), .SrcSel(cpu_controller_1_srcsel), .DstSel(cpu_controller_1_dstsel),
    .AluOp(cpu_controller_1_aluop), .MemCtrl(DataCtrl));
  alu alu_1 (
    .Source(DataAddr), .Out(alu_1_out), .Op(cpu_controller_1_aluop), .Destination(register_bank_1_dstout));  // open: Zero
  Controlled_Buffer #(.width(16)) controlled_buffer_1 (.in(register_bank_1_dstout), .out(DataData));  // open: en
  Controlled_Buffer #(.width(16)) controlled_buffer_2 (.in(alu_1_out), .out(DataData));  // open: en
  Pull_Resistor pull_resistor_1 (.node(DataData));
  Pull_Resistor pull_resistor_2 (.node(DataAddr));

  // Notes on the sheet:
  //   DataBus
  //   AddressBus
endmodule
